# Fritzing sketch hub75&rs485 (saved by Fritzing 0.9.3b)
circuit board: 10.3417cm x 5.48972cm

parts:
  J1 = shrouded pin header, 16 pins [form="♂ (shrouded male)"]
  Part1 = Arduino Mega ADK (Rev3)

nets:
  N1: J1.pin1, Part1.D24
  N2: J1.pin2, Part1.D26
  N3: J1.pin3, Part1.D27
  N4: J1.pin4, Part1.D29
  N5: J1.pin5, Part1.A0
  N6: J1.pin6, Part1.A2
  N7: J1.pin7, Part1.D11_PWM
  N8: J1.pin8, Part1.D9_PWM
  N9: J1.pin9, J1.pin13, J1.pin15, Part1.GND
  N10: J1.pin10, Part1.D10_PWM
  N11: J1.pin11, Part1.A3
  N12: J1.pin12, Part1.A1
  N13: J1.pin14, Part1.D28
  N14: J1.pin16, Part1.D25
